# Fritzing sketch project2Fritzing (saved by Fritzing 0.9.4)
stripboards: 1

parts:
  M2 = DC Motor
  VCC1 = 4 x AAA Battery Mount
  HC-SR04_Sensor_1 = HC-SR04 Ultrasonic Distance Sensor
  M1 = DC Motor
  U6 = TCM8240MD [package=tcm8240md]  # not connected
  MCU1 = Raspberry Pi B+  # not connected
  U7 = TCRT5000 [package=THT]
  U8 = TCRT5000 [package=THT]
  U9 = TCRT5000 [package=THT]
  U10 = TCRT5000 [package=THT]
  Part1 = Adafruit DC+Stepper Motor HAT [part_number="Adafruit #2348"]

nets:
  N1: M2.pin_1, Part1.M2A
  N2: M2.pin_2, Part1.M2B
  GND: VCC1.-, HC-SR04_Sensor_1.GND, Part1.GND
  N3: VCC1.+, Part1.VMOTOR
  N4: HC-SR04_Sensor_1.VCC, Part1.5.0V
  N5: HC-SR04_Sensor_1.TRIG, Part1.GPIO26
  N6: HC-SR04_Sensor_1.ECHO, Part1.GPIO19
  N7: M1.pin_1, Part1.M1B
  N8: M1.pin_2, Part1.M1A
  N9: U7.Pin_1, U7.Pin_2
  N10: U7.Pin_3, U7.Pin_4
  N11: U8.Pin_1, U8.Pin_2
  N12: U8.Pin_3, U8.Pin_4
  N13: U9.Pin_1, U9.Pin_2
  N14: U9.Pin_3, U9.Pin_4
  N15: U10.Pin_1, U10.Pin_2
  N16: U10.Pin_3, U10.Pin_4

custom parts:
  TCRT5000: TCRT5000 optical reflective sensor
  Adafruit DC+Stepper Motor HAT: Let your robotic dreams come true with the new DC+Stepper Motor HAT from Adafruit. This Raspberry Pi add-on is perfect for any motion project as it can drive up to 4 DC or 2 Stepper motors with full PWM speed control. Since the Raspberry Pi does not have a lot of PWM pins, we use a fully-dedicated PWM driver chip onboard to both control motor direction and speed. This chip handles all the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
